# Fritzing sketch CYEN132Final_Project_Circuit_Layout (saved by Fritzing 0.9.3b)
breadboards: 1

parts:
  Raspberry_Pi_1 = Raspberry Pi 3 [part_number=RPI-3-V1.2]
  LED4 = LED - 5mm [color="Red (633nm)" package="5 mm [THT]"]
  LED5 = LED - 5mm [color="Yellow (595nm)" package="5 mm [THT]"]
  LED6 = LED - 5mm [color="Yellow (595nm)" package="5 mm [THT]"]
  LED7 = LED - 5mm [color="Yellow (595nm)" package="5 mm [THT]"]
  LED8 = LED - 5mm [color="Yellow (595nm)" package="5 mm [THT]"]
  LED9 = LED - 5mm [color="Yellow (595nm)" package="5 mm [THT]"]
  LED10 = LED - 5mm [color="Yellow (595nm)" package="5 mm [THT]"]
  LED11 = LED - 5mm [color="Green (555nm)" package="5 mm [THT]"]
  LED12 = LED - 5mm [color="Yellow (595nm)" package="5 mm [THT]"]
  R1 = Resistor [tolerance=±5% resistance=220 package=THT]
  R2 = Resistor [tolerance=±5% resistance=220 package=THT]
  R3 = Resistor [tolerance=±5% resistance=220 package=THT]
  R4 = Resistor [tolerance=±5% resistance=220 package=THT]
  R5 = Resistor [tolerance=±5% resistance=220 package=THT]
  R6 = Resistor [tolerance=±5% resistance=220 package=THT]
  R7 = Resistor [tolerance=±5% resistance=220 package=THT]
  R8 = Resistor [tolerance=±5% resistance=220 package=THT]
  R9 = Resistor [tolerance=±5% resistance=220 package=THT]
  Power_plug1 = Power plug  # not connected

nets:
  N1: Raspberry_Pi_1.GPIO17, LED9.cathode
  N2: Raspberry_Pi_1.GPIO27, LED10.cathode
  N3: Raspberry_Pi_1.GPIO22, LED6.cathode
  N4: Raspberry_Pi_1.GPIO6, LED12.cathode
  N5: Raspberry_Pi_1.GPIO13, LED4.cathode
  N6: Raspberry_Pi_1.GPIO26, LED11.cathode
  N7: Raspberry_Pi_1.GPIO21, LED5.cathode
  N8: Raspberry_Pi_1.GPIO20, LED7.cathode
  N9: Raspberry_Pi_1.GPIO16, LED8.cathode
  N10: Raspberry_Pi_1.GND, R1.Pin_1, R2.Pin_1, R3.Pin_1, R4.Pin_1, R5.Pin_1, R6.Pin_1, R7.Pin_1, R8.Pin_1, R9.Pin_1
  N11: LED4.anode, R1.Pin_0
  N12: LED5.anode, R6.Pin_0
  N13: LED6.anode, R5.Pin_0
  N14: LED7.anode, R7.Pin_0
  N15: LED8.anode, R8.Pin_0
  N16: LED9.anode, R3.Pin_0
  N17: LED10.anode, R4.Pin_0
  N18: LED11.anode, R9.Pin_0
  N19: LED12.anode, R2.Pin_0
